// Logisim project compare.circ as structural Verilog: 4 circuits, main circuit comp_8bit
module comp_1bit (
  input  A,
  input  B,
  output Less,
  output Equal,
  output Greater
);

  wire not_1_out, not_2_out;

  not not_1 (not_1_out, A);
  not not_2 (not_2_out, B);
  and and_1 (Less, not_1_out, B);
  and and_2 (Greater, A, not_2_out);
  nor nor_1 (Equal, Less, Greater);
endmodule

module comp_2bit (
  input  [1:0] A,
  input  [1:0] B,
  output LT,
  output EQ,
  output GT
);

  wire and_1_out, and_2_out, and_3_out, and_4_out, and_5_out, and_6_out, not_1_out, not_2_out, not_3_out,
       not_4_out, xnor_1_out, xnor_2_out;

  not not_1 (not_1_out, A[1]);
  not not_2 (not_2_out, A[0]);
  not not_3 (not_3_out, B[0]);
  not not_4 (not_4_out, B[1]);
  and and_1 (and_1_out, B[1], not_1_out);
  and and_2 (and_2_out, not_1_out, not_2_out, B[0]);
  and and_3 (and_3_out, not_2_out, B[1], B[0]);
  xnor xnor_1 (xnor_1_out, A[0], B[0]);
  xnor xnor_2 (xnor_2_out, A[1], B[1]);
  and and_4 (and_4_out, A[1], not_4_out);
  and and_5 (and_5_out, A[0], not_4_out, not_3_out);
  and and_6 (and_6_out, A[1], A[0], not_3_out);
  or or_1 (LT, and_1_out, and_2_out, and_3_out);
  and and_7 (EQ, xnor_1_out, xnor_2_out);
  or or_2 (GT, and_4_out, and_5_out, and_6_out);

  // Notes on the sheet:
  //   A1
  //   B1
  //   A0
  //   B0
endmodule

module comp_4bit (
  input  [3:0] A,
  input  [3:0] B,
  input  iLT,
  input  iEQ,
  input  iGT,
  output LT,
  output EQ,
  output GT
);

  wire and_1_out, and_2_out, and_3_out, and_4_out, and_5_out, and_6_out, and_8_out, and_9_out, and_10_out,
       and_11_out, not_1_out, not_2_out, not_3_out, not_4_out, not_5_out, not_6_out, not_7_out, not_8_out,
       or_1_out, or_2_out, xnor_1_out, xnor_2_out, xnor_3_out, xnor_4_out;

  not not_1 (not_1_out, A[3]);
  // Probe on A
  not not_2 (not_2_out, A[1]);
  not not_3 (not_3_out, A[2]);
  not not_4 (not_4_out, A[0]);
  // Probe on B
  not not_5 (not_5_out, B[2]);
  not not_6 (not_6_out, B[3]);
  not not_7 (not_7_out, B[0]);
  not not_8 (not_8_out, B[1]);
  Pull_Resistor pull_resistor_1 (.node(iLT));
  Pull_Resistor #(.pull(1)) pull_resistor_2 (.node(iEQ));
  Pull_Resistor pull_resistor_3 (.node(iGT));
  xnor xnor_1 (xnor_1_out, A[3], B[3]);
  xnor xnor_2 (xnor_2_out, A[2], B[2]);
  xnor xnor_3 (xnor_3_out, A[1], B[1]);
  xnor xnor_4 (xnor_4_out, A[0], B[0]);
  and and_1 (and_1_out, not_1_out, B[3]);
  and and_2 (and_2_out, not_3_out, B[2], xnor_1_out);
  and and_3 (and_3_out, A[3], not_6_out);
  and and_4 (and_4_out, A[2], not_5_out, xnor_1_out);
  and and_5 (and_5_out, not_2_out, B[1], xnor_1_out, xnor_2_out);
  and and_6 (and_6_out, not_4_out, B[0], xnor_1_out, xnor_2_out, xnor_3_out);
  and and_7 (EQ, iEQ, xnor_1_out, xnor_2_out, xnor_3_out, xnor_4_out);
  and and_8 (and_8_out, A[1], not_8_out, xnor_2_out, xnor_1_out);
  and and_9 (and_9_out, A[0], not_7_out, xnor_2_out, xnor_3_out, xnor_1_out);
  or or_1 (or_1_out, and_1_out, and_2_out, and_5_out, and_6_out);
  or or_2 (or_2_out, and_3_out, and_4_out, and_8_out, and_9_out);
  and and_10 (and_10_out, iEQ, or_1_out);
  and and_11 (and_11_out, or_2_out, iEQ);
  or or_3 (LT, iLT, and_10_out);
  or or_4 (GT, and_11_out, iGT);

  // Notes on the sheet:
  //   A3
  //   A1
  //   A2
  //   A0
  //   B3
  //   B1
  //   B2
  //   B0
endmodule

module comp_8bit (
  input  [7:0] A,
  input  [7:0] B,
  output LT,
  output EQ,
  output GT
);

  wire comp_4bit_1_eq, comp_4bit_1_gt, comp_4bit_1_lt;

  comp_4bit comp_4bit_1 (
    .A(A[7:4]), .B(B[7:4]), .iLT(1'b0), .iEQ(1'b1), .iGT(1'b0), .LT(comp_4bit_1_lt), .EQ(comp_4bit_1_eq),
    .GT(comp_4bit_1_gt));
  comp_4bit comp_4bit_2 (
    .A(A[3:0]), .B(B[3:0]), .iLT(comp_4bit_1_lt), .iEQ(comp_4bit_1_eq), .iGT(comp_4bit_1_gt), .LT(LT),
    .EQ(EQ), .GT(GT));
endmodule
