// Logisim project shifter.circ as structural Verilog: 2 circuits, main circuit shifter_4bit
module shifter_4bit (
  input  SHL,
  input  [3:0] D,
  input  [2:0] S,
  input  CE,
  input  OE,
  output [3:0] O
);

  wire and_4_out, and_5_out, and_6_out, and_7_out, and_8_out, and_9_out, and_10_out, not_1_out, not_2_out,
       not_3_out, not_4_out;
  wire [2:0] notS;
  wire [3:0] controlled_buffer_1_out, controlled_buffer_4_out, controlled_buffer_7_out;

  not not_1 (not_1_out, S[0]);
  not not_2 (not_2_out, S[1]);
  not not_3 (not_3_out, S[2]);
  not not_4 (not_4_out, SHL);
  and and_1 (notS[0], CE, not_1_out);
  and and_2 (notS[1], CE, not_2_out);
  and and_3 (notS[2], CE, not_3_out);
  and and_4 (and_4_out, CE, OE);
  and and_5 (and_5_out, CE, SHL, S[0]);
  assign controlled_buffer_1_out = and_5_out ? {D[2:0], 1'b0} : 4'bz;  // Controlled_Buffer controlled_buffer_1
  assign controlled_buffer_1_out = notS[0] ? D : 4'bz;  // Controlled_Buffer controlled_buffer_2
  assign controlled_buffer_1_out = and_6_out ? {1'b0, D[3:1]} : 4'bz;  // Controlled_Buffer controlled_buffer_3
  and and_6 (and_6_out, CE, not_4_out, S[0]);
  and and_7 (and_7_out, CE, SHL, S[1]);
  assign controlled_buffer_4_out = and_7_out ? {controlled_buffer_1_out[1:0], 2'b00} : 4'bz;  // Controlled_Buffer controlled_buffer_4
  assign controlled_buffer_4_out = notS[1] ? controlled_buffer_1_out : 4'bz;  // Controlled_Buffer controlled_buffer_5
  assign controlled_buffer_4_out = and_8_out ? {2'b00, controlled_buffer_1_out[3:2]} : 4'bz;  // Controlled_Buffer controlled_buffer_6
  and and_8 (and_8_out, CE, not_4_out, S[1]);
  and and_9 (and_9_out, CE, SHL, S[2]);
  assign controlled_buffer_7_out = and_9_out ? 4'b0000 : 4'bz;  // Controlled_Buffer controlled_buffer_7
  assign controlled_buffer_7_out = notS[2] ? controlled_buffer_4_out : 4'bz;  // Controlled_Buffer controlled_buffer_8
  assign controlled_buffer_7_out = and_10_out ? 4'b0000 : 4'bz;  // Controlled_Buffer controlled_buffer_9
  and and_10 (and_10_out, CE, not_4_out, S[2]);
  assign O = and_4_out ? controlled_buffer_7_out : 4'bz;  // Controlled_Buffer controlled_buffer_10

  // Notes on the sheet:
  //   Left - 1
  //   No Shift
  //   Right - 1
  //   Left - 2
  //   Right - 2
  //   Left - 4
  //   Right - 4
endmodule

module shifter_8bit (
  input  SHL,
  input  [7:0] D,
  input  [3:0] S,
  input  CE,
  input  OE,
  output [7:0] O
);

  wire and_5_out, and_6_out, and_7_out, and_8_out, and_9_out, and_10_out, and_11_out, and_12_out, and_13_out,
       not_1_out, not_2_out, not_3_out, not_4_out, not_5_out;
  wire [3:0] notS;
  wire [7:0] controlled_buffer_1_out, controlled_buffer_4_out, controlled_buffer_7_out,
       controlled_buffer_10_out;

  not not_1 (not_1_out, SHL);
  and and_1 (notS[0], CE, not_2_out);
  not not_2 (not_2_out, S[0]);
  and and_2 (notS[1], CE, not_3_out);
  not not_3 (not_3_out, S[1]);
  and and_3 (notS[2], CE, not_4_out);
  not not_4 (not_4_out, S[2]);
  and and_4 (notS[3], CE, not_5_out);
  not not_5 (not_5_out, S[3]);
  and and_5 (and_5_out, CE, OE);
  and and_6 (and_6_out, CE, SHL, S[0]);
  assign controlled_buffer_1_out = and_6_out ? {D[6:0], 1'b0} : 8'bz;  // Controlled_Buffer controlled_buffer_1
  assign controlled_buffer_1_out = notS[0] ? D : 8'bz;  // Controlled_Buffer controlled_buffer_2
  assign controlled_buffer_1_out = and_7_out ? {1'b0, D[7:1]} : 8'bz;  // Controlled_Buffer controlled_buffer_3
  and and_7 (and_7_out, not_1_out, S[0], CE);
  and and_8 (and_8_out, CE, SHL, S[1]);
  assign controlled_buffer_4_out = and_8_out ? {controlled_buffer_1_out[5:0], 2'b00} : 8'bz;  // Controlled_Buffer controlled_buffer_4
  assign controlled_buffer_4_out = notS[1] ? controlled_buffer_1_out : 8'bz;  // Controlled_Buffer controlled_buffer_5
  assign controlled_buffer_4_out = and_9_out ? {2'b00, controlled_buffer_1_out[7:2]} : 8'bz;  // Controlled_Buffer controlled_buffer_6
  and and_9 (and_9_out, not_1_out, S[1], CE);
  and and_10 (and_10_out, CE, SHL, S[2]);
  assign controlled_buffer_7_out = and_10_out ? {controlled_buffer_4_out[3:0], 4'b0000} : 8'bz;  // Controlled_Buffer controlled_buffer_7
  assign controlled_buffer_7_out = notS[2] ? controlled_buffer_4_out : 8'bz;  // Controlled_Buffer controlled_buffer_8
  assign controlled_buffer_7_out = and_11_out ? {4'b0000, controlled_buffer_4_out[7:4]} : 8'bz;  // Controlled_Buffer controlled_buffer_9
  and and_11 (and_11_out, not_1_out, S[2], CE);
  and and_12 (and_12_out, CE, SHL, S[3]);
  assign controlled_buffer_10_out = and_12_out ? {8{1'b0}} : 8'bz;  // Controlled_Buffer controlled_buffer_10
  assign controlled_buffer_10_out = notS[3] ? controlled_buffer_7_out : 8'bz;  // Controlled_Buffer controlled_buffer_11
  assign controlled_buffer_10_out = and_13_out ? {8{1'b0}} : 8'bz;  // Controlled_Buffer controlled_buffer_12
  and and_13 (and_13_out, not_1_out, S[3], CE);
  assign O = and_5_out ? controlled_buffer_10_out : 8'bz;  // Controlled_Buffer controlled_buffer_13

  // Notes on the sheet:
  //   Left - 1
  //   No Shift
  //   Right - 1
  //   Left - 2
  //   Right - 2
  //   Left - 4
  //   Right - 4
  //   Left - 8
  //   Right - 8
endmodule
