// Logisim project tristate.circ as structural Verilog: 1 circuit, main circuit main
module main (
  input  en,
  input  A,
  output O
);

  assign O = en ? A : 1'bz;  // Controlled_Buffer controlled_buffer_1
endmodule
